# Fritzing sketch MQTT Bed Control box (saved by Fritzing 0.9.3b)
breadboards: 1

parts:
  WeMos_D1_Mini1 = WeMos D1 Mini  # not connected
  Q1 = NPN-Transistor [package="TO92 [THT]"]
  R3 = Resistor [tolerance=±5% resistance=220 package="1206 [SMD]"]
  D1 = Rectifier Diode [package="Melf DO-213 AA [SMD]"]
  U2 = RELAY [package=relay-g5q]
  U1 = Optocoupler [package=THT]
  U3 = Optocoupler [package=THT]
  Q2 = NPN-Transistor [package="TO92 [THT]"]
  R4 = Resistor [tolerance=±5% resistance=220 package="1206 [SMD]"]
  D2 = Rectifier Diode [package="Melf DO-213 AA [SMD]"]
  U4 = RELAY [package=relay-g5q]
  J1 = Camdenboss CTB0158-4 [part_number=CTB0158-4 package=THT]

nets:
  N1: Q1.E, U2.COIL2, U1.Pin_2, Q2.E, U4.COIL2
  N2: Q1.B, R3.Pin_1
  N3: Q1.C, D1.anode, U2.COIL1
  N4: R3.Pin_0, U1.Pin_5
  N5: D1.cathode, U1.Pin_4, U3.Pin_4
  N6: U2.MAIN, J1.pin1
  N7: U2.NO, J1.pin2
  N8: U3.Pin_5, R4.Pin_0
  N9: Q2.B, R4.Pin_1
  N10: Q2.C, D2.anode, U4.COIL1
  N11: U4.MAIN, J1.pin3
  N12: U4.NO, J1.pin4

notes:
  Relay 2 NO Relay Contacts
  Relay 1 NO Relay Contacts
  The items below are all contained in the module specified in parts section. There is no need to put together individual components. This scematic is just for reference.
